# Fritzing sketch FootSwitch3 (saved by Fritzing 0.9.3b)
stripboards: 1

parts:
  Solo_LED = LED - 5mm [color="Red (633nm)" package="5 mm [THT]"]
  Solo_Switch = Toggle Switch [package=THT]
  Ch2_LED = LED - 5mm [color="Orange (620nm)" package="5 mm [THT]"]
  Ch1_LED = LED - 5mm [color="Blue (525nm)" package="5 mm [THT]"]
  Amp_Switch = SWITCH-DPDT [package=gpi-152-3013]
  Ethernet_Jack = female pin header, 8 pins [form="♀ (female)"]
  R1 = Resistor [tolerance=±5% resistance=250 package=THT]
  Ethernet_Jack2 = female pin header, 8 pins [form="♀ (female)"]
  U1 = 941H-2C-5D [package=relay-5v]
  U2 = 941H-2C-5D [package=relay-5v]
  U3 = 941H-2C-5D [package=relay-5v]
  AMP_LED = RGB LED (com. cathode, rgb) [package="5 mm [THT]"]
  IC1 = IC, DIP package, 8 pins [chip_label=IC]
  D1 = Rectifier Diode [part_number=1N4001 package="300 mil [THT]"]
  D2 = Rectifier Diode [part_number=1N4001 package="300 mil [THT]"]
  C1 = Electrolytic Capacitor [capacitance=1µF package="100 mil [THT, electrolytic]"]
  C2 = Electrolytic Capacitor [capacitance=1µF package="100 mil [THT, electrolytic]"]
  C3 = Electrolytic Capacitor [capacitance=1µF package="100 mil [THT, electrolytic]"]
  C4 = Electrolytic Capacitor [capacitance=1µF package="100 mil [THT, electrolytic]"]
  Power_plug1 = Power plug
  Ch3 = SWITCH-DPDT [package=gpi-152-3013]
  Ch2 = SWITCH-DPDT [package=gpi-152-3013]
  Ch1 = SWITCH-DPDT [package=gpi-152-3013]
  R2 = Resistor [tolerance=±5% resistance=270 package=THT]
  Reverb_Switch = Toggle Switch [package=THT]
  Solo_LED1 = LED - 5mm [color="Blue (505nm)" package="5 mm [THT]"]
  J1 = female pin header, 5 pins [form="♀ (female)"]
  J2 = female pin header, 2 pins [form="♀ (female)"]
  Ch3_LED = LED - 5mm [color="Red (633nm)" package="5 mm [THT]"]

nets:
  N1: Solo_LED.cathode, Ch2_LED.cathode, Ch1_LED.anode, AMP_LED.common_cathode, R2.Pin_0, Solo_LED1.cathode, Ch3_LED.cathode
  N2: Solo_LED.anode, Solo_Switch.L2
  N3: Solo_Switch.L1, Ethernet_Jack.pin4
  N4: Solo_Switch.COM, Amp_Switch.2, Amp_Switch.5, Ethernet_Jack.pin1, U1.6, Ch3.3, Ch2.3, Ch2.6, Ch1.3, Reverb_Switch.COM
  N5: Ch2_LED.anode, U1.11
  N6: Ch1_LED.cathode, U1.9, Ch3_LED.anode
  N7: Amp_Switch.1, AMP_LED.red_anode, AMP_LED.green_anode
  N8: Amp_Switch.3, AMP_LED.blue_anode
  N9: Amp_Switch.6, Ethernet_Jack.pin3
  N10: Ethernet_Jack.pin2, U1.1
  N11: Ethernet_Jack.pin5, Reverb_Switch.L1
  N12: Ethernet_Jack.pin6, Ch3.5, Ch2.5
  N13: Ethernet_Jack.pin7, Ch2.2, Ch1.2
  N14: Ethernet_Jack.pin8, R2.Pin_1
  N15: R1.Pin_0, U1.8
  N16: R1.Pin_1, U1.16
  9V: Ethernet_Jack2.pin1, U2.9, IC1.pin1, IC1.pin8, D2.anode, Power_plug1.VCC
  N17: Ethernet_Jack2.pin2, U3.11
  N18: Ethernet_Jack2.pin3, J1.pin1
  N19: Ethernet_Jack2.pin4, J1.pin2
  N20: Ethernet_Jack2.pin5, J1.pin3
  N21: Ethernet_Jack2.pin6, J1.pin4
  N22: Ethernet_Jack2.pin7, J1.pin5
  GND: Ethernet_Jack2.pin8, U2.1, U3.1, IC1.pin3, C1.-, C4.-, Power_plug1.GND
  N23: U1.4, U1.13
  -9V: U2.11, IC1.pin5, C4.+
  N24: U2.13, U3.13
  N25: U2.16, J2.pin2
  N26: U3.16, J2.pin1
  N27: IC1.pin2, C2.+, C3.-
  N28: IC1.pin4, C2.-
  18V: D1.cathode, C1.+
  N29: D1.anode, D2.cathode, C3.+
  N30: Reverb_Switch.L2, Solo_LED1.anode

custom parts:
  941H-2C-5D: DPDT Relay - 2 Form C
