# Fritzing sketch PowerSwitches (saved by Fritzing 0.9.3b)
stripboards: 2

parts:
  Solo_LED = LED - 5mm [color="Red (633nm)" package="5 mm [THT]"]  # not connected
  Solo_LED1 = LED - 5mm [color="Blue (505nm)" package="5 mm [THT]"]  # not connected
  R6 = Resistor [tolerance=±5% resistance=220 package=THT]  # not connected
  R7 = Resistor [tolerance=±10% resistance=220 package=THT]  # not connected
  U6 = RELAY-2 [package=relay-g5v]  # not connected
  U7 = RELAY-2 [package=relay-g5v]
  R8 = Resistor [tolerance=±10% resistance=180 package=THT]
  S1 = Pushbutton [package=THT]
  J1 = female pin header, 2 pins [form="♀ (female)"]
  J2 = female pin header, 2 pins [form="♀ (female)"]
  LED1 = RGB LED (com. cathode, rgb) [package="5 mm [THT]"]

nets:
  N1: U7.2, R8.Pin_0
  9V: U7.5
  N2: U7.9, LED1.red_anode
  N3: U7.10, J2.pin1
  N4: R8.Pin_1, S1.leg0, J1.pin1
  12V: S1.leg1
  GND: J1.pin2, J2.pin2, LED1.common_cathode
