# Fritzing sketch SignalManager (saved by Fritzing 0.9.3b)
circuit board: 8.46667cm x 5.64444cm
stripboards: 1

parts:
  U4 = 941H-2C-5D [package=relay-5v]
  U5 = LM 358 Dual Op-Amp [package="DIP8 [THT]"]
  U6 = 941H-2C-5D [package=relay-5v]
  U7 = LM 358 Dual Op-Amp [package="DIP8 [THT]"]
  R3 = Resistor [tolerance=±5% resistance=220 package=THT]
  R4 = Resistor [tolerance=±5% resistance=220 package=THT]
  U8 = 941H-2C-5D [package=relay-5v]
  U9 = 941H-2C-5D [package=relay-5v]
  U10 = LM 358 Dual Op-Amp [package="DIP8 [THT]"]
  R5 = Resistor [tolerance=±5% resistance=220 package=THT]
  J1 = female pin header, 4 pins [form="♀ (female)"]
  J2 = female pin header, 5 pins [form="♀ (female)"]
  Effects_Return = Audio Jack (TRS) 3.5mm [package="4Ucon 08780 [THT]"]
  ToMesaInput = Audio Jack (TRS) 3.5mm [package="4Ucon 08780 [THT]"]
  ToOrangeInput = Audio Jack (TRS) 3.5mm [package="4Ucon 08780 [THT]"]
  R1 = Rotary Potentiometer (Large) [maximum_resistance=100kΩ package=THT]
  ToPihranaInput = Audio Jack (TRS) 3.5mm [package="4Ucon 08780 [THT]"]
  R2 = Rotary Potentiometer (Large) [maximum_resistance=100kΩ package=THT]
  Effects_Return_2 = Audio Jack (TRS) 3.5mm [package="4Ucon 08780 [THT]"]
  Master_Input = Audio Jack (TRS) 3.5mm [package="4Ucon 08780 [THT]"]
  OrangeOut = Audio Jack (TRS) 3.5mm [package="4Ucon 08780 [THT]"]
  PihranaOut = Audio Jack (TRS) 3.5mm [package="4Ucon 08780 [THT]"]
  ToEffects = Audio Jack (TRS) 3.5mm [package="4Ucon 08780 [THT]"]
  MesaOut = Audio Jack (TRS) 3.5mm [package="4Ucon 08780 [THT]"]

nets:
  N1: U4.1, J1.pin4
  N2: U4.4, ToMesaInput.Ring
  N3: U4.6, U5.connector2, U5.connector4, Master_Input.Ring
  N4: U4.8, U5.connector5, U5.connector6
  N5: U4.9, U8.11, U9.6, R5.Pin_1
  N6: U4.11, R1.leg1, MesaOut.Ring
  N7: U4.13, Effects_Return.Ring
  GND: U4.16, U6.16, U8.16, U9.1, J2.pin1, ToMesaInput.Sleeve, ToOrangeInput.Sleeve, R1.leg2, ToPihranaInput.Sleeve, R2.leg1, Effects_Return_2.Sleeve, Master_Input.Sleeve, OrangeOut.Sleeve, PihranaOut.Sleeve, ToEffects.Sleeve, MesaOut.Sleeve
  N8: U5.connector0, U5.connector1, U6.8
  -9V: U5.connector3, U7.connector3, U10.connector3, J2.pin2
  9V: U5.connector7, U7.connector7, U10.connector7, J2.pin4
  N9: U6.1, J1.pin3
  N10: U6.4, ToOrangeInput.Ring
  N11: U6.6, ToPihranaInput.Ring
  N12: U6.9, R2.leg2
  N13: U6.11, PihranaOut.Ring
  N14: U6.13, OrangeOut.Ring
  N15: U7.connector0, U7.connector1, R3.Pin_1
  N16: U7.connector2, R2.wiper
  N17: U7.connector4, R1.wiper
  N18: U7.connector5, U7.connector6, R4.Pin_1
  N19: R3.Pin_0, U8.13
  N20: R4.Pin_0, U9.4
  N21: U8.1, J1.pin1
  N22: U8.9, U9.8, ToEffects.Ring
  N23: U9.16, J1.pin2
  N24: U10.connector0, U10.connector1, R5.Pin_0
  N25: U10.connector2, Effects_Return_2.Ring

custom parts:
  941H-2C-5D: DPDT Relay - 2 Form C
