# Fritzing sketch SignalManager2 (saved by Fritzing 0.9.3b)
stripboards: 1

parts:
  U4 = 941H-2C-5D [package=relay-5v]
  U5 = LM 358 Dual Op-Amp [package="DIP8 [THT]"]
  U6 = 941H-2C-5D [package=relay-5v]
  U7 = LM 358 Dual Op-Amp [package="DIP8 [THT]"]
  R4 = Resistor [tolerance=±5% resistance=220 package=THT]
  U8 = 941H-2C-5D [package=relay-5v]
  U9 = 941H-2C-5D [package=relay-5v]
  Effects_Return = Audio Jack (TRS) 3.5mm [package="4Ucon 08780 [THT]"]
  ToMesaInput = Audio Jack (TRS) 3.5mm [package="4Ucon 08780 [THT]"]
  ToOrangeInput = Audio Jack (TRS) 3.5mm [package="4Ucon 08780 [THT]"]
  ToPihranaInput = Audio Jack (TRS) 3.5mm [package="4Ucon 08780 [THT]"]
  Effects_Return_2 = Audio Jack (TRS) 3.5mm [package="4Ucon 08780 [THT]"]
  Master_Input = Audio Jack (TRS) 3.5mm [package="4Ucon 08780 [THT]"]
  OrangeOut = Audio Jack (TRS) 3.5mm [package="4Ucon 08780 [THT]"]
  PihranaOut = Audio Jack (TRS) 3.5mm [package="4Ucon 08780 [THT]"]
  ToEffects = Audio Jack (TRS) 3.5mm [package="4Ucon 08780 [THT]"]
  MesaOut = Audio Jack (TRS) 3.5mm [package="4Ucon 08780 [THT]"]
  J3 = female pin header, 2 pins [form="♀ (female)"]
  R8 = Resistor [tolerance=±5% resistance=100 package=THT]
  R9 = Resistor [tolerance=±5% resistance=100 package=THT]
  R11 = Resistor [tolerance=±5% resistance=1k package=THT]
  R13 = Resistor [tolerance=±5% resistance=47k package=THT]
  J5 = female pin header, 2 pins [form="♀ (female)"]
  J6 = male pin header, 2 pins [form="♂ (male)"]
  J9 = female pin header, 2 pins [form="♀ (female)"]
  J10 = male pin header, 2 pins [form="♂ (male)"]
  J8 = male pin header, 2 pins [form="♂ (male)"]
  J7 = female pin header, 2 pins [form="♀ (female)"]
  J11 = female pin header, 2 pins [form="♀ (female)"]
  J12 = male pin header, 2 pins [form="♂ (male)"]
  J13 = female pin header, 2 pins [form="♀ (female)"]
  J14 = male pin header, 2 pins [form="♂ (male)"]
  J15 = female pin header, 2 pins [form="♀ (female)"]
  J16 = male pin header, 2 pins [form="♂ (male)"]
  J17 = female pin header, 2 pins [form="♀ (female)"]
  J18 = male pin header, 2 pins [form="♂ (male)"]
  J19 = female pin header, 2 pins [form="♀ (female)"]
  J20 = male pin header, 2 pins [form="♂ (male)"]
  J21 = female pin header, 2 pins [form="♀ (female)"]
  J22 = male pin header, 2 pins [form="♂ (male)"]
  J1 = female pin header, 2 pins [form="♀ (female)"]
  R2 = Rotary Potentiometer (Large) [maximum_resistance=10kΩ package=THT]
  Effects_Blend = Rotary Potentiometer (Large) [maximum_resistance=10kΩ package=THT]
  J23 = female pin header, 2 pins [form="♀ (female)"]
  J26 = female pin header, 3 pins [form="♀ (female)"]
  J27 = male pin header, 3 pins [form="♂ (male)"]
  J2 = male pin header, 3 pins [form="♂ (male)"]
  J28 = male pin header, 5 pins [form="♂ (male)"]
  J29 = male pin header, 3 pins [form="♂ (male)"]
  J30 = female pin header, 3 pins [form="♀ (female)"]
  R12 = Resistor [tolerance=±5% resistance=47k package=THT]
  R10 = Resistor [tolerance=±5% resistance=1k package=THT]
  U11 = LM 358 Dual Op-Amp [package="DIP8 [THT]"]
  R3 = Resistor [tolerance=±5% resistance=220 package=THT]
  J4 = male pin header, 2 pins [form="♂ (male)"]

nets:
  GND: U4.1, U4.9, U6.1, U8.1, U9.1, R8.Pin_1, R9.Pin_1, J6.pin2, J10.pin2, J8.pin2, J12.pin2, J14.pin2, J16.pin2, J18.pin2, J20.pin2, J22.pin2, J2.pin1, J28.pin1, J29.pin2, J4.pin2
  N1: U4.4, J18.pin1
  N2: U4.6, U5.connector6, J14.pin1, U11.connector4
  N3: U4.8, J26.pin2
  N4: U4.11, U5.connector2, J16.pin1
  N5: U4.13, J4.pin1
  N6: U4.16, J23.pin2
  N7: U5.connector0, U5.connector1, U6.8
  -9V: U5.connector3, U7.connector3, J2.pin2, J28.pin2, U11.connector3
  9V: U5.connector7, U7.connector7, J2.pin3, J28.pin4, U11.connector7
  N8: U6.4, J6.pin1
  N9: U6.6, J8.pin1
  N10: U6.9, U11.connector2
  N11: U6.11, J10.pin1
  N12: U6.13, J12.pin1
  N13: U6.16, J23.pin1
  N14: U7.connector0, R10.Pin_0, R3.Pin_1
  N15: U7.connector1, R8.Pin_0, R10.Pin_1
  N16: U7.connector2, J29.pin1, R12.Pin_0
  N17: U7.connector4, R13.Pin_0, J29.pin3
  N18: U7.connector5, R9.Pin_0, R11.Pin_1
  N19: U7.connector6, R4.Pin_1, R11.Pin_0
  N20: R4.Pin_0, U9.13
  N21: U8.9, U9.9, J20.pin1
  N22: U8.11, U9.11, J26.pin1
  N23: U8.13, R3.Pin_0
  N24: U8.16, J1.pin1
  N25: U9.16, J1.pin2
  N26: Effects_Return.Sleeve, J17.pin2
  N27: Effects_Return.Ring, J17.pin1
  N28: ToMesaInput.Sleeve, J3.pin2
  N29: ToMesaInput.Ring, J3.pin1
  N30: ToOrangeInput.Sleeve, J5.pin2
  N31: ToOrangeInput.Ring, J5.pin1
  N32: ToPihranaInput.Sleeve, J7.pin2
  N33: ToPihranaInput.Ring, J7.pin1
  N34: Effects_Return_2.Sleeve, J21.pin2
  N35: Effects_Return_2.Ring, J21.pin1
  N36: Master_Input.Sleeve, J15.pin2
  N37: Master_Input.Ring, J15.pin1
  N38: OrangeOut.Sleeve, J11.pin2
  N39: OrangeOut.Ring, J11.pin1
  N40: PihranaOut.Sleeve, J9.pin2
  N41: PihranaOut.Ring, J9.pin1
  N42: ToEffects.Sleeve, J19.pin2
  N43: ToEffects.Ring, J19.pin1
  N44: MesaOut.Sleeve, J13.pin2
  N45: MesaOut.Ring, J13.pin1
  N46: R13.Pin_1, U11.connector5, U11.connector6
  N47: J22.pin1, J26.pin3
  N48: R2.leg1, J30.pin3
  N49: R2.wiper, J30.pin2
  N50: R2.leg2, J30.pin1
  N51: Effects_Blend.leg1, J27.pin1
  N52: Effects_Blend.wiper, J27.pin2
  N53: Effects_Blend.leg2, J27.pin3
  N54: R12.Pin_1, U11.connector0, U11.connector1

custom parts:
  941H-2C-5D: DPDT Relay - 2 Form C
